# Fritzing sketch Esquema_Fritzing (saved by Fritzing 1.0.1rc)
breadboards: 1

parts:
  Orange_Pi_One1 = Orange Pi One [part_number=OPI-ONE]
  S1 = Pushbutton [package="[THT]"]
  R1 = Resistor [tolerance=±5% power=0.25W resistance=10k package=THT]
  C1 = Ceramic Capacitor [capacitance=100nF voltage=35V package="100 mil [THT, multilayer]"]

nets:
  N1: Orange_Pi_One1.3v3, R1.Pin_1
  N2: Orange_Pi_One1.GND, S1.Pin_3, S1.Pin_4, C1.1
  N3: Orange_Pi_One1.PA10, S1.Pin_1, S1.Pin_2, R1.Pin_0, C1.0

custom parts:
  Orange Pi One: It’s an open-source single-board computer. It can run Android 4.4, Ubuntu, Debian, Rasberry Pi Image, as well as the banana pi Image. It uses the AllWinner H3 SoC, and has 512MB DDR3 SDRAM
